// Logisim project Logicism 4 bits adder.circ as structural Verilog: 1 circuit, main circuit main
module main (
  input  A1,
  input  A4,
  input  A3,
  input  A2,
  input  B4,
  input  B3,
  input  B2,
  input  B1,
  output C4,
  output S4,
  output S3,
  output S2,
  output S1
);

  wire adder_1_cout, adder_2_cout, adder_3_cout;

  Adder #(.width(1)) adder_1 (.a(A1), .b(B1), .out(S1), .cout(adder_1_cout));  // open: cin
  Adder #(.width(1)) adder_2 (.a(A2), .b(B2), .out(S2), .cin(adder_1_cout), .cout(adder_2_cout));
  Adder #(.width(1)) adder_3 (.a(A3), .b(B3), .out(S3), .cin(adder_2_cout), .cout(adder_3_cout));
  Adder #(.width(1)) adder_4 (.a(A4), .b(B4), .out(S4), .cin(adder_3_cout), .cout(C4));
endmodule
